// Digital circuit astro_genius.dig as structural Verilog
module astro_genius (
  input  _1_Hz,
  input  _10000_Hz,
  input  _10000_Hz_2,
  input  _1_Hz_2,
  input  _10000_Hz_3,
  input  _1000_Hz,
  input  in_19,
  input  [7:0] in_20,
  input  in_21,
  output Pronto,
  output [4:0] Jogo_principal,
  output [4:0] Coordena,
  output [4:0] Compara_tiros_e_asteroides,
  output [4:0] Move_tiros,
  output [4:0] Compara_asteroides__nave_e_tiros,
  output [4:0] Move_asteroides,
  output [3:0] Registra_tiros,
  output E,
  output out_16,
  output [4:0] out_17,
  output [5:0] out_18
);

  wire button_1_out, button_2_out, Iniciar_out, Reset_2_out, Reset_out, switch_1_b, switch_5_b;
  wire [3:0] u_astro_genius_db_pontos, u_astro_genius_db_vidas, u_astro_genius_matriz_y,
       u_jogo_base_db_asteroide_x, u_jogo_base_db_asteroide_y, u_jogo_base_db_pontos, u_jogo_base_db_tiro_x,
       u_jogo_base_db_tiro_y, u_jogo_base_db_vidas, u_jogo_base_matriz_y;
  wire [5:0] SHIFT_out, UP_2_out;
  wire [14:0] u_astro_genius_matriz_x, u_jogo_base_matriz_x;

  Button UP (.out(SHIFT_out[5]));
  Button DOWN (.out(SHIFT_out[4]));
  Button LEFT (.out(SHIFT_out[3]));
  Button RIGHT (.out(SHIFT_out[2]));
  Switch switch_1 (.A(_1000_Hz), .B(switch_1_b));
  Switch switch_2 (.A(_1_Hz_2), .B(switch_1_b));
  Switch switch_3 (.A(_10000_Hz_3), .B(switch_1_b));
  Button button_1 (.out(button_1_out));
  Switch switch_4 (.A(button_1_out), .B(switch_1_b));
  Button Reset (.out(Reset_out));
  Button SHIFT (.out(SHIFT_out[0]));
  Button S (.out(SHIFT_out[1]));
  astro_genius #(.applicationType("IVERILOG")) u_astro_genius (
    .clock(switch_1_b), .reset(Reset_out), .chaves(SHIFT_out), .saida_serial(out_16),
    .matriz_x(u_astro_genius_matriz_x), .matriz_y(u_astro_genius_matriz_y),
    .db_vidas(u_astro_genius_db_vidas), .db_pontos(u_astro_genius_db_pontos), .db_uc_menu(out_17),
    .wire_saida_reg_jogada(out_18));
  LedMatrix #(.ledPersistence("true"), .colAddrBits(4), .rowDataBits(15)) ledmatrix_1 (
    .rows(u_astro_genius_matriz_x), .column(u_astro_genius_matriz_y));
  Seven_Seg_Hex seven_seg_hex_1 (.d(u_astro_genius_db_pontos), .dp(1'b0));
  Seven_Seg_Hex seven_seg_hex_2 (.d(u_astro_genius_db_vidas), .dp(1'b0));
  Switch switch_5 (.A(_10000_Hz_2), .B(switch_5_b));
  Switch switch_6 (.A(_1_Hz), .B(switch_5_b));
  Switch switch_7 (.A(_10000_Hz), .B(switch_5_b));
  Button button_2 (.out(button_2_out));
  Switch switch_8 (.A(button_2_out), .B(switch_5_b));
  Button Reset_2 (.out(Reset_2_out));
  Button Iniciar (.out(Iniciar_out));
  Button UP_2 (.out(UP_2_out[5]));
  Button DOWN_2 (.out(UP_2_out[4]));
  Button LEFT_2 (.out(UP_2_out[3]));
  Button RIGHT_2 (.out(UP_2_out[2]));
  Button S_2 (.out(UP_2_out[1]));
  Button SHIFT_2 (.out(UP_2_out[0]));
  jogo_base #(.applicationType("IVERILOG")) u_jogo_base (
    .clock(switch_5_b), .reset(Reset_2_out), .iniciar(Iniciar_out), .chaves(UP_2_out),
    .jogo_base_em_andamento(in_19), .tela_renderizar(in_20), .iniciar_transmissao(in_21), .gameover(Pronto),
    .db_estado_jogo_principal(Jogo_principal), .db_estado_coordena_asteroides_tiros(Coordena),
    .db_estado_compara_tiros_e_asteroide(Compara_tiros_e_asteroides), .db_estado_move_tiros(Move_tiros),
    .db_estado_compara_asteroides_com_nave_e_tiros(Compara_asteroides__nave_e_tiros),
    .db_estado_move_asteroides(Move_asteroides), .db_estado_registra_tiro(Registra_tiros),
    .matriz_x(u_jogo_base_matriz_x), .matriz_y(u_jogo_base_matriz_y), .db_vidas(u_jogo_base_db_vidas),
    .db_pontos(u_jogo_base_db_pontos), .db_tiro_x(u_jogo_base_db_tiro_x), .db_tiro_y(u_jogo_base_db_tiro_y),
    .db_asteroide_x(u_jogo_base_db_asteroide_x), .db_asteroide_y(u_jogo_base_db_asteroide_y), .db_especial(E));  // open: db_estado_uc_gera_frame, db_estado_uc_renderiza, db_uc_gera_asteroide, db_up, db_down, db_left, db_right, db_estado_registra_tiro_especial, db_estado_uc_envia_dados, acabou_transmissao, saida_serial
  Seven_Seg_Hex seven_seg_hex_3 (.d(u_jogo_base_db_asteroide_x), .dp(1'b0));
  Seven_Seg_Hex seven_seg_hex_4 (.d(u_jogo_base_db_asteroide_y), .dp(1'b0));
  LedMatrix #(.ledPersistence("true"), .colAddrBits(4), .rowDataBits(15)) ledmatrix_2 (
    .rows(u_jogo_base_matriz_x), .column(u_jogo_base_matriz_y));
  Seven_Seg_Hex seven_seg_hex_5 (.d(u_jogo_base_db_tiro_x), .dp(1'b0));
  Seven_Seg_Hex seven_seg_hex_6 (.d(u_jogo_base_db_tiro_y), .dp(1'b0));
  Seven_Seg_Hex seven_seg_hex_7 (.d(u_jogo_base_db_pontos), .dp(1'b0));
  Seven_Seg_Hex seven_seg_hex_8 (.d(u_jogo_base_db_vidas), .dp(1'b0));

  // Notes on the sheet:
  //   _10000_Hz: Hz: 10000
  //   _10000_Hz_2: Hz: 10000
  //   _10000_Hz_3: Hz: 10000
  //   _1000_Hz: Hz: 1000
  //   uc menu
  //   pontos
  //   vidas
  //   asteroides
  //   x
  //   y
  //   tiros
endmodule

/* Code of astro_genius:
module astro_genius (
    input clock,
    input reset,
    input [5:0] chaves,
    output saida_serial,

    /* sinais de depuracao * /
    output [14:0] matriz_x,
    output [3:0] matriz_y,
    // displays
    output [3:0] db_vidas,
    output [3:0] db_pontos,
    output [4:0] db_uc_menu,
    output [5:0] wire_saida_reg_jogada
);

wire wire_reset;
wire wire_iniciar_jogo;
wire wire_gameover;
wire wire_jogo_base_em_andamento;

uc_menu uc_menu (
    /*input* /
    .reset(reset),
    .clock(clock),
    .ocorreu_jogada(wire_ocorreu_jogada),
    .tiro(wire_saida_reg_jogada[0]),
    .especial(wire_saida_reg_jogada[1]),
    // .fim_envia_dados(wire_fim_envia_dados), // sem serializacao
    .fim_envia_dados(1'b1), // com serialização
    .pronto(wire_gameover),
        /*output* /
    .reset_reg_jogada(wire_reset_reg_jogada),
    .enable_reg_jogada(wire_enable_reg_jogada),
    .envia_dados(wire_envia_dados),
    .iniciar(wire_iniciar_jogo),
    .jogo_base_em_andamento(wire_jogo_base_em_andamento),
    .reset_jogo_base(wire_reset),
    .tela_renderizada(wire_tela_renderizada), // 8 b bits
    .db_estado_uc_menu(db_uc_menu)
);

wire wire_envia_dados;
wire [7:0] wire_tela_renderizada;
wire wire_fim_envia_dados;




wire wire_enable_reg_jogada;
wire wire_reset_reg_jogada;
wire [5:0] wire_saida_reg_jogada;
registrador_n #(6) reg_jogada (
    /* inputs * /
    .clock  (clock),
    .clear  (wire_reset_reg_jogada),
    .enable (wire_enable_reg_jogada),
    .D      (chaves),
    /* output * /
    .Q      (wire_saida_reg_jogada)
); 

wire wire_ocorreu_jogada;

or (wire_ocorreu_jogada, wire_ocorreu_tiro, wire_ocorreu_especial);

wire wire_ocorreu_tiro, wire_ocorreu_especial; 

edge_detector edge_detector_tiro(
    /*inputs* /
    .clock(clock),
    .reset(1'b0),
    .sinal(chaves[0]),
    /*output* /
    .pulso(wire_ocorreu_tiro)
);

edge_detector edge_detector_especial(
    /*inputs* /
    .clock(clock),
    .reset(1'b0),
    .sinal(chaves[1]),
    /*output* /
    .pulso(wire_ocorreu_especial)
);

jogo_base jogo_base(
    /* inputs * /
    .clock(clock),
    .reset(wire_reset),
    .iniciar(wire_iniciar_jogo),
    .chaves(chaves),
    .jogo_base_em_andamento(wire_jogo_base_em_andamento),
    .tela_renderizar(wire_tela_renderizada),
    .iniciar_transmissao(wire_envia_dados),


    /* outputs * /
    .gameover(wire_gameover),
    /* sinais de depuracao * /
    .db_estado_jogo_principal(),
    .db_estado_coordena_asteroides_tiros(),
    .db_estado_compara_tiros_e_asteroide(),
    .db_estado_move_tiros(),
    .db_estado_compara_asteroides_com_nave_e_tiros(),
    .db_estado_move_asteroides(),
    .db_estado_registra_tiro(),
    .db_estado_uc_gera_frame(),
    .db_estado_uc_renderiza(),
    .db_uc_gera_asteroide(),
    .matriz_x(matriz_x),
    .matriz_y(matriz_y),
    //displays
    .db_vidas(db_vidas),
    .db_pontos(db_pontos),
    .db_tiro_x(),
    .db_tiro_y(),
    .db_asteroide_x(),
    .db_asteroide_y(),
    .db_up(),
    .db_down(),
    .db_left(),
    .db_right(),
    .db_estado_registra_tiro_especial(),
    .db_especial(),
    .db_estado_uc_envia_dados(),
    .acabou_transmissao(wire_fim_envia_dados),
    .saida_serial(saida_serial)
);

endmodule

module jogo_base (
    input clock,
    input reset,
    input iniciar,
    input [5:0] chaves,
    input jogo_base_em_andamento,
    input [7:0] tela_renderizar,
    input iniciar_transmissao,
    output gameover,
    /* sinais de depuracao * /
    output [4:0] db_estado_jogo_principal,
    output [4:0] db_estado_coordena_asteroides_tiros,
    output [4:0] db_estado_compara_tiros_e_asteroide,
    output [4:0] db_estado_move_tiros,
    output [4:0] db_estado_compara_asteroides_com_nave_e_tiros,
    output [4:0] db_estado_move_asteroides,
    output [3:0] db_estado_registra_tiro,
    output [3:0] db_estado_uc_gera_frame,
    output [3:0] db_estado_uc_renderiza,
    output [3:0] db_uc_gera_asteroide,
    output [14:0] matriz_x,
    output [3:0] matriz_y,
    //displays
    output [3:0] db_vidas,
    output [3:0] db_pontos,
    output [3:0] db_tiro_x,
    output [3:0] db_tiro_y,
    output [3:0] db_asteroide_x,
    output [3:0] db_asteroide_y,
    output db_up,
    output db_down,
    output db_left,
    output db_right,
    output [3:0] db_estado_registra_tiro_especial,
    output db_especial,
    output [5:0] db_estado_uc_envia_dados,
    output acabou_transmissao,
    output saida_serial
);


assign db_up = chaves[5];
assign db_down = chaves[4];
assign db_left = chaves[3];
assign db_right = chaves[2];

wire wire_vidas;
wire wire_fim_movimentacao_asteroides_e_tiros;
wire wire_inicia_registra_tiros;
wire wire_inicia_movimentacao_asteroides_e_tiros;
wire wire_reset_maquinas;
wire wire_reset_contador_asteroides_uc_principal;
wire wire_reset_contador_tiro_uc_principal; 
wire wire_enable_decrementador; 
wire wire_reset_contador_vidas;
wire wire_ocorreu_tiro;
wire wire_ocorreu_jogada;
wire wire_reset_reg_jogada;
wire wire_enable_reg_jogada;
wire wire_destruido_aste;
wire [3:0] wire_aste_coor_x;
wire [3:0] wire_aste_coor_y;
wire [1:0] wire_opcode_mux_out;
wire wire_reset_pontuacao_uc_principal;
wire wire_termina_uc_jogo_principal;
wire wire_fim_registra_especial;
wire wire_wire_ocorreu_tiro;
wire wire_tiro;
wire wire_especial;
wire wire_inicia_registra_especial;
wire wire_wire_reset_pontuacao;
wire wire_rco_intervalo_tiro;
wire wire_reset_contador_tiro_uc_registra_especial;
wire wire_reset_contador_especial_uc_registra_especial;
wire wire_enable_mem_tiro_uc_registra_especial;
wire wire_new_load_uc_registra_especial;
wire wire_conta_contador_opcode;
wire wire_conta_contador_tiro_uc_registra_especial;
wire wire_select_mux_especial_opcode;


/******************************************************************************************************************** /
/*********************************************UC_ENVIA_DADOS.V****************************************************** /
/******************************************************************************************************************** /

wire wire_conta_contador_aste_uc_envia_dados;
wire wire_reset_contador_aste_uc_envia_dados;
wire wire_conta_contador_tiro_uc_envia_dados;
wire wire_reset_contador_tiro_uc_envia_dados;
wire wire_iniciar_transmissao_uart_tx;
wire wire_terminou_de_enviar_dados_uc_envia_dados;
wire wire_terminou_transmissao_de_byte;
uc_envia_dados uc_envia_dados(
    /* inputs * /
    .clock(clock),
    .reset(wire_reset_maquinas),
    .enviar_dados(wire_enviar_dados_uc_coordena_asteroides_tiros),
    .acabou_transmissao_uart_tx(wire_terminou_transmissao_de_byte),
    .rco_contador_aste(wire_rco_contador_asteroides),
    .rco_contador_tiros(wire_rco_contador_tiro),
    .rco_contador_byte_opcode(wire_rco_contador_byte_opcode),
    .rco_contador_rodape(wire_rco_contador_rodape),
    /* outputs * /
    .iniciar_transmissao_uart_tx(wire_iniciar_transmissao_uart_tx),
    .enable_reg_opcode(wire_enable_reg_opcode),
    .reset_reg_opcode(wire_reset_reg_opcode),
    .conta_contador_byte_opcode(wire_conta_contador_byte_opcode),
    .reset_contador_byte_opcode(wire_reset_contador_byte_opcode),
    .conta_contador_mux_byte_enviar(wire_conta_contador_mux_byte_enviar),
    .reset_contador_mux_byte_enviar(wire_reset_contador_mux_byte_enviar),
    .conta_contador_aste(wire_conta_contador_aste_uc_envia_dados),
    .reset_contador_aste(wire_reset_contador_aste_uc_envia_dados),
    .conta_contador_tiro(wire_conta_contador_tiro_uc_envia_dados),
    .reset_contador_tiro(wire_reset_contador_tiro_uc_envia_dados),
    .conta_contador_rodape(wire_conta_contador_rodape),
    .reset_contador_rodape(wire_reset_contador_rodape),
    .terminou_de_enviar_dados(wire_terminou_de_enviar_dados_uc_envia_dados),
    .esta_enviando_pos_asteroides(wire_esta_enviando_pos_asteroides),
    .db_estado_uc_envia_dados(db_estado_uc_envia_dados)
    );

wire wire_reset_reg_opcode;
wire wire_enable_reg_opcode;
wire wire_esta_enviando_pos_asteroides;
wire [31:0] wire_opcode_enviar;

/*Registrador para os enivar os 4 bytes de opcode de tiros / asteroides* /
registrador_n #(32) reg_opcode (
    .clock(clock),
    .clear(wire_reset_reg_opcode),
    .enable(wire_enable_reg_opcode),
    .D(wire_esta_enviando_pos_asteroides ? {wire_opcode_enviar[31:2], wire_opcode_aste} : {wire_opcode_enviar[31:2], wire_opcode_tiro}),
    .Q(wire_opcode_enviar)
);

wire wire_conta_contador_byte_opcode;
wire wire_reset_contador_byte_opcode;
wire [1:0]  select_mux_byte_opcode;
wire wire_rco_contador_byte_opcode;

/*contador utilizado como seletor do mux de byte opcode* /
contador_m #(4, 2) contador_byte_opcode
  (
   .clock(clock),
   .zera_as(wire_reset_contador_byte_opcode || wire_reset_maquinas),
   .zera_s(1'b0),
   .conta(wire_conta_contador_byte_opcode),
   .Q(select_mux_byte_opcode),
   .fim(wire_rco_contador_byte_opcode),
   .meio()
  );
wire [7:0] byte_opcode_enviar;
/*mux utilziado para selecionar o byte de opcode a ser enviado* /
assign byte_opcode_enviar = select_mux_byte_opcode == 2'b00 ? wire_opcode_enviar[31:24] :
                            select_mux_byte_opcode == 2'b01 ? wire_opcode_enviar[23:16] :
                            select_mux_byte_opcode == 2'b10 ? wire_opcode_enviar[15:8]  : wire_opcode_enviar[7:0];

wire wire_conta_contador_mux_byte_enviar;
wire wire_reset_contador_mux_byte_enviar;
wire [3:0] select_mux_byte_enviar;
/*contador utilizado como seletor do mux de byte enviar* /
contador_m #(8, 4) contador_byte_enviar
  (
   .clock(clock),
   .zera_as(wire_reset_contador_mux_byte_enviar),
   .zera_s(1'b0),
   .conta(wire_conta_contador_mux_byte_enviar),
   .Q(select_mux_byte_enviar),
   .fim(),
   .meio()
  );

wire [7:0] byte_enviar;
assign byte_enviar = (select_mux_byte_enviar == 4'd0) ? wire_pontos_aux[7:0] :
                     (select_mux_byte_enviar == 4'd1) ? {wire_opcode_mux_out, wire_quantidade_vidas, 3'b000} :
                     (select_mux_byte_enviar == 4'd2) ? {(wire_aste_renderizado ? {wire_aste_coor_x, wire_aste_coor_y} : 8'b0)} :
                     (select_mux_byte_enviar == 4'd3) ? byte_opcode_enviar :
                     (select_mux_byte_enviar == 4'd4) ? {(wire_tiro_renderizado ? {wire_tiro_coor_x, wire_tiro_coor_y} : 8'b0)} :
                     (select_mux_byte_enviar == 4'd5) ? byte_opcode_enviar : 
                     (select_mux_byte_enviar == 4'd6) ? {wire_saida_reg_jogada[1], wire_rco_intervalo_especial, wire_saida_reg_jogada[0], wire_rco_intervalo_tiro, wire_vidas, 3'b0} : 
                     (select_mux_byte_enviar == 4'd7) ? {4'd4, 4'd1} : {wire_pontos_aux[7:0]};

wire wire_conta_contador_rodape;
wire wire_reset_contador_rodape;
wire wire_rco_contador_rodape;

/*contador utilizado para mandar o rodapé* /
contador_m #(2, 2) contador_rodape
  (
   .clock(clock),
   .zera_as(wire_reset_contador_rodape),
   .zera_s(1'b0),
   .conta(wire_conta_contador_rodape),
   .Q(),
   .fim(wire_rco_contador_rodape),
   .meio()
  );

uart_tx #(3) UART_TX_INST (
    .i_Clock(clock),
    .i_Tx_DV(jogo_base_em_andamento ? wire_iniciar_transmissao_uart_tx : iniciar_transmissao), // sinal de iniciar a transmissão
    .i_Tx_Byte(jogo_base_em_andamento ? byte_enviar : tela_renderizar),                    // dado
    .o_Tx_Active(),                             // sinal que indica que a uart de transmitir dados está ocupada
    .o_Tx_Serial(saida_serial),
    .o_Tx_Done(wire_terminou_transmissao_de_byte)   // pronto
);
assign acabou_transmissao = wire_terminou_transmissao_de_byte;

/******************************************************************************************************************** /
/*********************************************UC_JOGO_PRINCIPAL****************************************************** /
/******************************************************************************************************************** /
wire wire_ocorreu_especial;
uc_jogo_principal uc_jogo_principal(
    /* inputs * /
    .clock(clock),
    .iniciar(iniciar),
    .reset(reset),
    .vidas(~wire_vidas),
    .fim_movimentacao_asteroides_e_tiros(wire_fim_movimentacao_asteroides_e_tiros), 
    .fim_registra_tiros(wire_tiro_registrado),
    .fim_registra_especial(wire_fim_registra_especial),
    .ocorreu_tiro(wire_ocorreu_tiro),
    .ocorreu_jogada(wire_ocorreu_jogada),
    .ocorreu_especial(wire_ocorreu_especial),
    .tiro(wire_saida_reg_jogada[0]),
    .especial(wire_saida_reg_jogada[1]),
    .rco_intervalo_especial(wire_rco_intervalo_especial),
    .rco_intervalo_tiro(wire_rco_intervalo_tiro),
    /* outputs * /
    .enable_reg_jogada(wire_enable_reg_jogada),
    .reset_reg_jogada(wire_reset_reg_jogada),
    .reset_pontuacao(wire_reset_pontuacao_uc_principal),
    .inicia_registra_tiros(wire_inicia_registra_tiros),
    .inicia_registra_especial(wire_inicia_registra_especial),
    .inicia_movimentacao_asteroides_e_tiros(wire_inicia_movimentacao_asteroides_e_tiros), 
    .reset_contador_asteroides(wire_reset_contador_asteroides_uc_principal),
    .reset_contador_tiro(wire_reset_contador_tiro_uc_principal),
    .reset_contador_vidas(wire_reset_contador_vidas),
    .reset_maquinas(wire_reset_maquinas),
    .pronto(gameover),
    .termina(wire_termina_uc_jogo_principal),
    .db_estado_jogo_principal(db_estado_jogo_principal)
);

contador_163 #(64) contador_intervalo_tiro  ( 
    /* inputs * /
    .clock(clock),
    .clr(wire_tiro_registrado || wire_reset_maquinas),
    .ld(1'b0),
    .ent(1'b1),
    .enp(1'b1), 
    .D(),
    .Max(64'd250),
    /*outputs* /
    .Q(),
    .rco(wire_rco_intervalo_tiro)
);

wire [1:0] wire_opcode_especial;
wire wire_enable_load_tiro_uc_registra_especial;
wire wire_select_mux_pos_uc_registra_especial;
wire [1:0] wire_select_mux_pos_tiro_uc_registra_especial;


/******************************************************************************************************************** /
/*********************************************UC_REGISTRA_ESPECIAL*************************************************** /
/******************************************************************************************************************** /

uc_registra_especial uc_registra_especial(
    /* inputs * /
    .clock(clock),
    .reset(wire_reset_maquinas),
    .registra_tiro_especial(wire_inicia_registra_especial), 
    .loaded_tiro(wire_tiro_renderizado),
    .rco_contador_tiro(wire_rco_contador_tiro),
    .rco_opcode(wire_rco_contador_especial),
    /* outputs * /
    .reset_contador_tiro(wire_reset_contador_tiro_uc_registra_especial), 
    .reset_contador_especial(wire_reset_contador_especial_uc_registra_especial),
    .reset_intervalo_especial(wire_reset_intervalo_especial),
    .enable_mem_tiro(wire_enable_mem_tiro_uc_registra_especial), 
    .select_mux_pos(wire_select_mux_pos_tiro_uc_registra_especial),
    .new_load(wire_new_load_uc_registra_especial),
    .enable_load_tiro(wire_enable_load_tiro_uc_registra_especial),
    .conta_contador_opcode(wire_conta_contador_opcode),
    .conta_contador_tiro(wire_conta_contador_tiro_uc_registra_especial),
    .especial_registrado(wire_fim_registra_especial), 
    .select_mux_especial_opcode(wire_select_mux_especial_opcode),
    .db_estado_registra_tiro_especial(db_estado_registra_tiro_especial)
);


mux_reg_jogada mux_jogada(
    .select_mux_jogada (wire_saida_reg_jogada[5:2]),
    /* output * /
    .saida_mux       (wire_opcode_mux_out)
);

/**********mux para o seletor do opcode para registrar o tiro*************** /
wire [1:0] wire_opcode_registra_tiro;
assign wire_opcode_registra_tiro = wire_select_mux_especial_opcode ?  wire_opcode_contador_especial : wire_opcode_mux_out;

wire wire_rco_contador_especial;
wire [1:0] wire_opcode_contador_especial;

contador_m #(4, 2) contador_tiro_especial_opcode (
    /* inputs * /
    .clock(clock),
    .zera_as(wire_reset_contador_especial_uc_registra_especial || wire_reset_maquinas),
    .zera_s(1'b0),
    .conta(wire_conta_contador_opcode),
    /* outputs * /
    .Q(wire_opcode_contador_especial),
    .fim(wire_rco_contador_especial),
    .meio()
);

wire wire_rco_contador_tiro;
wire wire_rco_contador_asteroides;
wire wire_fim_move_tiros;
wire wire_fim_move_asteroides;
wire wire_fim_comparacao_asteroides_com_a_nave_e_tiros;
wire wire_fim_comparacao_tiros_e_asteroides;
wire wire_movimenta_tiro;
wire wire_sinal_movimenta_asteroides;
wire wire_sinal_compara_tiros_e_asteroides_uc_coordena_asteroides_tiros;
wire wire_sinal_compara_asteroides_com_a_nave_e_tiro;
wire wire_sinal_compara_tiros_e_asteroide_uc_compara_asteroides_com_nave_e_tiros;
wire wire_inicia_gera_frame_uc_coordena_asteroides_tiros;
wire wire_fim_gera_frame_uc_gera_frame;
wire wire_pausar_renderizacao;
wire wire_gera_asteroide;
wire wire_rco_contador_gera_aste;
wire reset_contador_gera_aste;


/******************************************************************************************************************** /
/**************************************************DIFICULDADES****************************************************** /
/******************************************************************************************************************** /
wire wire_rco_contador_movimenta_tiro;
wire wire_rco_contador_movimenta_asteroide;
wire wire_reset_contador_movimenta_tiro;
wire wire_reset_contador_movimenta_asteroide;



parameter tempo_especial = 64'd20000;

wire [63:0] tempo_gera_aste;
wire [63:0] tempo_move_aste;
wire [63:0] tempo_move_tiro;


contador_163_dificuldades #(64, 10000) contador_163_dificuldades( 
    .clock(clock), 
    .clr(iniciar || wire_reset_maquinas), 
    .ld(1'b0), 
    .ent(1'b1), 
    .enp(1'b1), 
    .D(),
    .Q(), 
    .rco(),
    .tempo_gera_aste(tempo_gera_aste),
    .tempo_move_aste(tempo_move_aste),
    .tempo_move_tiro(tempo_move_tiro)
);


contador_163 #(64) contador_gera_asteroide  ( 
    /* inputs * /
    .clock(clock), 
    .clr(wire_reset_contador_gera_asteroide), 
    .ld(1'b0), 
    .ent(1'b1), 
    .enp(wire_conta_contador_gera_asteroide), 
    .D(),
    .Max(tempo_gera_aste),
    /* outputs * /
    .Q(),
    .rco(wire_rco_contador_gera_aste)
);

contador_163 #(64) contador_movimenta_tiro  ( 
    /* inputs * /
    .clock(clock), 
    .clr(wire_reset_contador_movimenta_tiro), 
    .ld(1'b0), 
    .ent(1'b1), 
    .enp(1'b1), 
    .D(),
    .Max(tempo_move_tiro),
    /*outputs* /
    .Q(),
    .rco(wire_rco_contador_movimenta_tiro)
);

contador_163 #(64) contador_movimenta_asteroide  ( 
    /* inputs * /
    .clock(clock), 
    .clr(wire_reset_contador_movimenta_asteroide), 
    .ld(1'b0), 
    .ent(1'b1), 
    .enp(1'b1), 
    .D(),
    .Max(tempo_move_aste),
    /*outputs* /
    .Q(),
    .rco(wire_rco_contador_movimenta_asteroide)
);

wire wire_reset_intervalo_especial;
wire wire_rco_intervalo_especial;
contador_163 #(64) contador_especial_163  ( 
    /* inputs * /
    .clock(clock), 
    .clr(wire_reset_intervalo_especial || wire_reset_maquinas), 
    .ld(1'b0), 
    .ent(1'b1), 
    .enp(1'b1), 
    .D(),
    .Max(tempo_especial),
    /*outputs* /
    .Q(),
    .rco(wire_rco_intervalo_especial)
);


assign db_especial = wire_rco_intervalo_especial;


/******************************************************************************************************************** /
/*********************************************UC_COORDENA_ASTEROIDES************************************************* /
/******************************************************************************************************************** /
wire wire_enviar_dados_uc_coordena_asteroides_tiros;
uc_coordena_asteroides_tiros uc_coordena_asteroides_tiros(
    /* inputs * /
    .clock(clock),
    .reset(wire_reset_maquinas),
    .move_tiro_e_asteroides(wire_inicia_movimentacao_asteroides_e_tiros),
    .rco_contador_movimenta_tiros(wire_rco_contador_movimenta_tiro),
    .rco_contador_movimenta_asteroides(wire_rco_contador_movimenta_asteroide),
    .fim_move_tiros(wire_fim_move_tiros),
    .fim_move_asteroides(wire_fim_move_asteroides),
    .fim_comparacao_asteroides_com_a_nave_e_tiros(wire_fim_comparacao_asteroides_com_a_nave_e_tiros),
    .fim_comparacao_tiros_e_asteroides(wire_fim_comparacao_tiros_e_asteroides),
    .fim_gera_frame(wire_fim_gera_frame_uc_gera_frame),
    .fim_gera_asteroide(wire_fim_gera_asteroide),
    // .fim_transmissao_de_dados(wire_terminou_de_enviar_dados_uc_envia_dados), // com a uart tx
    .fim_transmissao_de_dados(1'b1), // sem a uart tx
    .gera_aste(wire_rco_contador_gera_aste),
    .termina_operacao(wire_termina_uc_jogo_principal),
    /* outputs * /
    .movimenta_tiro(wire_movimenta_tiro),
    .sinal_movimenta_asteroides(wire_sinal_movimenta_asteroides),
    .sinal_compara_tiros_e_asteroides(wire_sinal_compara_tiros_e_asteroides_uc_coordena_asteroides_tiros ),
    .sinal_compara_asteroides_com_a_nave_e_tiro(wire_sinal_compara_asteroides_com_a_nave_e_tiro),
    .fim_move_tiro_e_asteroides(wire_fim_movimentacao_asteroides_e_tiros),
    .gera_frame(wire_inicia_gera_frame_uc_coordena_asteroides_tiros),
    .pausar_renderizacao(wire_pausar_renderizacao),
    .gera_asteroide(wire_gera_asteroide),
    .reset_gerador_random(wire_reset_gerador_random),
    .enviar_dados(wire_enviar_dados_uc_coordena_asteroides_tiros),
    .db_estado_coordena_asteroides_tiros(db_estado_coordena_asteroides_tiros)
);

wire wire_reset_contador_asteroides_uc_gera_asteroide;
wire wire_conta_contador_asteroides_uc_gera_asteroide;
wire wire_enable_mem_aste_uc_gera_asteroide;
wire wire_enable_load_aste_uc_gera_asteroide;
wire wire_new_loaded_aste_uc_gera_asteroide;
wire wire_conta_contador_gera_asteroide;
wire wire_reset_contador_gera_asteroide;



/******************************************************************************************************************** /
/*********************************************UC_GERA_ASTEROIDE****************************************************** /
/******************************************************************************************************************** /

uc_gera_asteroide uc_gera_asteroide (
    /* inputs * /
    .clock(clock)        ,
    .reset(wire_reset_maquinas),
    .gera_asteroide(wire_gera_asteroide),      
    .rco_contador_asteroide(wire_rco_contador_asteroides),
    .asteroide_renderizado(wire_aste_renderizado),

    /* outputs * /
    .reset_contador_asteroide(wire_reset_contador_asteroides_uc_gera_asteroide),
    .conta_contador_asteroide(wire_conta_contador_asteroides_uc_gera_asteroide),
    .conta_contador_gera_asteroide(wire_conta_contador_gera_asteroide),
    .reset_contador_gera_asteroide(wire_reset_contador_gera_asteroide),
    .enable_mem_aste(wire_enable_mem_aste_uc_gera_asteroide),
    .enable_load_aste(wire_enable_load_aste_uc_gera_asteroide),
    .new_loaded_aste(wire_new_loaded_aste_uc_gera_asteroide),
    .fim_gera_asteroide(wire_fim_gera_asteroide),
    .db_uc_gera_asteroide(db_uc_gera_asteroide)
);


wire wire_conta_contador_asteroides_uc_gera_frame;
wire wire_conta_contador_tiro_uc_gera_frame;
wire wire_reset_contador_tiro_uc_gera_frame;
wire wire_reset_contador_asteroide_uc_gera_frame;
wire wire_clear_mem_frame;
wire wire_enable_mem_frame;
wire [1:0] wire_select_mux_gera_frame;



/******************************************************************************************************************** /
/*************************************************UC_GERA_FRAME****************************************************** /
/******************************************************************************************************************** /

uc_gera_frame uc_gera_frame (
        /*inputs* /
        .clock(clock),
        .reset(wire_reset_maquinas),
        .gera_frame(wire_inicia_gera_frame_uc_coordena_asteroides_tiros),
        .rco_contador_asteroides(wire_rco_contador_asteroides),
        .rco_contador_tiro(wire_rco_contador_tiro),
        .loaded_tiro(wire_tiro_renderizado),
        .loaded_asteroide(wire_aste_renderizado),
        /*outputs* /
        .conta_contador_asteroide(wire_conta_contador_asteroides_uc_gera_frame),
        .conta_contador_tiro(wire_conta_contador_tiro_uc_gera_frame),
        .reset_contador_tiro(wire_reset_contador_tiro_uc_gera_frame),
        .reset_contador_asteroide(wire_reset_contador_asteroide_uc_gera_frame),
        .clear_mem_frame(wire_clear_mem_frame),
        .enable_mem_frame(wire_enable_mem_frame),
        .fim_gera_frame(wire_fim_gera_frame_uc_gera_frame),
        .select_mux_gera_frame(wire_select_mux_gera_frame),
        .db_estado_uc_gera_frame(db_estado_uc_gera_frame)
);


wire [3:0] wire_entrada_x_memoria_frame;
wire [3:0] wire_entrada_y_memoria_frame;

assign wire_entrada_x_memoria_frame = (wire_select_mux_gera_frame == 2'b00) ? wire_aste_coor_x : 
                                      (wire_select_mux_gera_frame == 2'b01) ? wire_tiro_coor_x : 
                                      (wire_select_mux_gera_frame == 2'b10) ? 4'b0111          : wire_saida_contador_frame ;
 
assign wire_entrada_y_memoria_frame = (wire_select_mux_gera_frame == 2'b00) ? wire_aste_coor_y : 
                                      (wire_select_mux_gera_frame == 2'b01) ? wire_tiro_coor_y :
                                      (wire_select_mux_gera_frame == 2'b10) ? 4'b0111          : wire_saida_contador_frame;

memoria_frame memoria_frame(
    /*inputs* /
    .coor_x(wire_entrada_y_memoria_frame),
    .coor_y(wire_entrada_x_memoria_frame),
    .clk   (clock),
    .clear(wire_clear_mem_frame),
    .we   (wire_enable_mem_frame),
    /*outputs* /
    .saida_x(matriz_x),
    .saida_y(matriz_y)
);

wire wire_rco_contador_frame;
wire wire_conta_contador_frame;
wire wire_reset_contador_frame;



/******************************************************************************************************************** /
/*********************************************UC_RENDERIZA****************************************************** /
/******************************************************************************************************************** /

wire [3:0] wire_saida_contador_frame; 
wire [3:0] entrada_y_mem_frame;

uc_renderiza uc_renderiza (
        /*inputs* /
        .clock(clock),
        .reset(wire_reset_maquinas),
        .pausar_renderizacao(wire_pausar_renderizacao),
        .rco_contador_frame(wire_rco_contador_frame),
        /*outputs* /
        .reset_contador_frame(wire_reset_contador_frame),
        .conta_contador_frame(wire_conta_contador_frame),
        .db_estado_uc_renderiza(db_estado_uc_renderiza)
);

 contador_m #(15, 4) contador_renderiza(
    /*inputs* /
   .clock(clock),
   .zera_as(wire_reset_contador_frame),
   .zera_s(1'b0),
   .conta(wire_conta_contador_frame),
   /*outputs* /
   .Q(wire_saida_contador_frame),
   .fim(wire_rco_contador_frame),
   .meio()
  );





/******************************************************************************************************************** /
/*************************************UC_COMPARA_TIROS_E_ASTEROIDES************************************************** /
/******************************************************************************************************************** /

wire wire_posicao_tiro_igual_asteroide;
wire wire_tiro_renderizado;
wire wire_aste_renderizado;
wire wire_reset_contador_asteroides_uc_compara_tiros_e_asteroides;
wire wire_reset_contador_tiros_uc_compara_tiros_e_asteroides;
wire wire_enable_load_tiro_uc_compara_tiros_e_asteroides;
wire wire_enable_load_asteroide_uc_compara_tiros_e_asteroides;
wire wire_new_loaded_tiro_uc_compara_tiros_e_asteroides;
wire wire_new_loaded_asteroide_uc_compara_tiros_e_asteroides;
wire wire_new_destruido_asteroide_uc_compara_tiros_e_asteroides;
wire wire_incrementa_pontos_uc_compara_tiros_e_asteroides;
wire wire_conta_contador_asteroides_uc_compara_tiros_e_asteroides;
wire wire_conta_contador_tiros_uc_compara_tiros_e_asteroides;

uc_compara_tiros_e_asteroides uc_compara_tiros_e_asteroides (
    /* inputs * /
    .clock(clock),
    .reset(wire_reset_maquinas),
    .compara_tiros_e_asteroides(wire_sinal_compara_tiros_e_asteroides_uc_coordena_asteroides_tiros |
                                wire_sinal_compara_tiros_e_asteroide_uc_compara_asteroides_com_nave_e_tiros
                                ),
    .posicao_tiro_igual_asteroide(wire_posicao_tiro_igual_asteroide),
    .rco_contador_asteroides(wire_rco_contador_asteroides),
    .rco_contador_tiros(wire_rco_contador_tiro),
    .tiro_renderizado(wire_tiro_renderizado),
    .aste_renderizado(wire_aste_renderizado),
    /* outputs * /
    .reset_contador_asteroides(wire_reset_contador_asteroides_uc_compara_tiros_e_asteroides),
    .reset_contador_tiros(wire_reset_contador_tiros_uc_compara_tiros_e_asteroides),
    .enable_load_tiro(wire_enable_load_tiro_uc_compara_tiros_e_asteroides),
    .enable_load_asteroide(wire_enable_load_asteroide_uc_compara_tiros_e_asteroides),
    .loaded_tiro(wire_new_loaded_tiro_uc_compara_tiros_e_asteroides),
    .loaded_asteroide(wire_new_loaded_asteroide_uc_compara_tiros_e_asteroides),
    .asteroide_destruido(wire_new_destruido_asteroide_uc_compara_tiros_e_asteroides),
    .conta_contador_asteroides(wire_conta_contador_asteroides_uc_compara_tiros_e_asteroides),
    .conta_contador_tiros(wire_conta_contador_tiros_uc_compara_tiros_e_asteroides),
    .incrementa_pontos(wire_incrementa_pontos_uc_compara_tiros_e_asteroides),
    .s_fim_comparacao(wire_fim_comparacao_tiros_e_asteroides),
    .db_estado_compara_tiros_e_asteroide(db_estado_compara_tiros_e_asteroide)
);


/******************************************************************************************************************** /
/*************************************************UC_MOVE_TIROS****************************************************** /
/******************************************************************************************************************** /

wire [1:0] wire_opcode_tiro;
wire wire_x_borda_max_tiro;
wire wire_y_borda_max_tiro;
wire wire_x_borda_min_tiro;
wire wire_y_borda_min_tiro;
wire [1:0] wire_select_mux_pos_tiro_uc_move_tiros;
wire wire_select_mux_coor_tiro_uc_move_tiros;
wire wire_select_soma_sub_uc_move_tiros;
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*/

/* Code of jogo_base:
module jogo_base (
    input clock,
    input reset,
    input iniciar,
    input [5:0] chaves,
    input jogo_base_em_andamento,
    input [7:0] tela_renderizar,
    input iniciar_transmissao,
    output gameover,
    /* sinais de depuracao * /
    output [4:0] db_estado_jogo_principal,
    output [4:0] db_estado_coordena_asteroides_tiros,
    output [4:0] db_estado_compara_tiros_e_asteroide,
    output [4:0] db_estado_move_tiros,
    output [4:0] db_estado_compara_asteroides_com_nave_e_tiros,
    output [4:0] db_estado_move_asteroides,
    output [3:0] db_estado_registra_tiro,
    output [3:0] db_estado_uc_gera_frame,
    output [3:0] db_estado_uc_renderiza,
    output [3:0] db_uc_gera_asteroide,
    output [14:0] matriz_x,
    output [3:0] matriz_y,
    //displays
    output [3:0] db_vidas,
    output [3:0] db_pontos,
    output [3:0] db_tiro_x,
    output [3:0] db_tiro_y,
    output [3:0] db_asteroide_x,
    output [3:0] db_asteroide_y,
    output db_up,
    output db_down,
    output db_left,
    output db_right,
    output [3:0] db_estado_registra_tiro_especial,
    output db_especial,
    output [5:0] db_estado_uc_envia_dados,
    output acabou_transmissao,
    output saida_serial
);


assign db_up = chaves[5];
assign db_down = chaves[4];
assign db_left = chaves[3];
assign db_right = chaves[2];

wire wire_vidas;
wire wire_fim_movimentacao_asteroides_e_tiros;
wire wire_inicia_registra_tiros;
wire wire_inicia_movimentacao_asteroides_e_tiros;
wire wire_reset_maquinas;
wire wire_reset_contador_asteroides_uc_principal;
wire wire_reset_contador_tiro_uc_principal; 
wire wire_enable_decrementador; 
wire wire_reset_contador_vidas;
wire wire_ocorreu_tiro;
wire wire_ocorreu_jogada;
wire wire_reset_reg_jogada;
wire wire_enable_reg_jogada;
wire wire_destruido_aste;
wire [3:0] wire_aste_coor_x;
wire [3:0] wire_aste_coor_y;
wire [1:0] wire_opcode_mux_out;
wire wire_reset_pontuacao_uc_principal;
wire wire_termina_uc_jogo_principal;
wire wire_fim_registra_especial;
wire wire_wire_ocorreu_tiro;
wire wire_tiro;
wire wire_especial;
wire wire_inicia_registra_especial;
wire wire_wire_reset_pontuacao;
wire wire_rco_intervalo_tiro;
wire wire_reset_contador_tiro_uc_registra_especial;
wire wire_reset_contador_especial_uc_registra_especial;
wire wire_enable_mem_tiro_uc_registra_especial;
wire wire_new_load_uc_registra_especial;
wire wire_conta_contador_opcode;
wire wire_conta_contador_tiro_uc_registra_especial;
wire wire_select_mux_especial_opcode;


/******************************************************************************************************************** /
/*********************************************UC_ENVIA_DADOS.V****************************************************** /
/******************************************************************************************************************** /

wire wire_conta_contador_aste_uc_envia_dados;
wire wire_reset_contador_aste_uc_envia_dados;
wire wire_conta_contador_tiro_uc_envia_dados;
wire wire_reset_contador_tiro_uc_envia_dados;
wire wire_iniciar_transmissao_uart_tx;
wire wire_terminou_de_enviar_dados_uc_envia_dados;
wire wire_terminou_transmissao_de_byte;
uc_envia_dados uc_envia_dados(
    /* inputs * /
    .clock(clock),
    .reset(wire_reset_maquinas),
    .enviar_dados(wire_enviar_dados_uc_coordena_asteroides_tiros),
    .acabou_transmissao_uart_tx(wire_terminou_transmissao_de_byte),
    .rco_contador_aste(wire_rco_contador_asteroides),
    .rco_contador_tiros(wire_rco_contador_tiro),
    .rco_contador_byte_opcode(wire_rco_contador_byte_opcode),
    .rco_contador_rodape(wire_rco_contador_rodape),
    /* outputs * /
    .iniciar_transmissao_uart_tx(wire_iniciar_transmissao_uart_tx),
    .enable_reg_opcode(wire_enable_reg_opcode),
    .reset_reg_opcode(wire_reset_reg_opcode),
    .conta_contador_byte_opcode(wire_conta_contador_byte_opcode),
    .reset_contador_byte_opcode(wire_reset_contador_byte_opcode),
    .conta_contador_mux_byte_enviar(wire_conta_contador_mux_byte_enviar),
    .reset_contador_mux_byte_enviar(wire_reset_contador_mux_byte_enviar),
    .conta_contador_aste(wire_conta_contador_aste_uc_envia_dados),
    .reset_contador_aste(wire_reset_contador_aste_uc_envia_dados),
    .conta_contador_tiro(wire_conta_contador_tiro_uc_envia_dados),
    .reset_contador_tiro(wire_reset_contador_tiro_uc_envia_dados),
    .conta_contador_rodape(wire_conta_contador_rodape),
    .reset_contador_rodape(wire_reset_contador_rodape),
    .terminou_de_enviar_dados(wire_terminou_de_enviar_dados_uc_envia_dados),
    .esta_enviando_pos_asteroides(wire_esta_enviando_pos_asteroides),
    .db_estado_uc_envia_dados(db_estado_uc_envia_dados)
    );

wire wire_reset_reg_opcode;
wire wire_enable_reg_opcode;
wire wire_esta_enviando_pos_asteroides;
wire [31:0] wire_opcode_enviar;

/*Registrador para os enivar os 4 bytes de opcode de tiros / asteroides* /
registrador_n #(32) reg_opcode (
    .clock(clock),
    .clear(wire_reset_reg_opcode),
    .enable(wire_enable_reg_opcode),
    .D(wire_esta_enviando_pos_asteroides ? {wire_opcode_enviar[31:2], wire_opcode_aste} : {wire_opcode_enviar[31:2], wire_opcode_tiro}),
    .Q(wire_opcode_enviar)
);

wire wire_conta_contador_byte_opcode;
wire wire_reset_contador_byte_opcode;
wire [1:0]  select_mux_byte_opcode;
wire wire_rco_contador_byte_opcode;

/*contador utilizado como seletor do mux de byte opcode* /
contador_m #(4, 2) contador_byte_opcode
  (
   .clock(clock),
   .zera_as(wire_reset_contador_byte_opcode || wire_reset_maquinas),
   .zera_s(1'b0),
   .conta(wire_conta_contador_byte_opcode),
   .Q(select_mux_byte_opcode),
   .fim(wire_rco_contador_byte_opcode),
   .meio()
  );
wire [7:0] byte_opcode_enviar;
/*mux utilziado para selecionar o byte de opcode a ser enviado* /
assign byte_opcode_enviar = select_mux_byte_opcode == 2'b00 ? wire_opcode_enviar[31:24] :
                            select_mux_byte_opcode == 2'b01 ? wire_opcode_enviar[23:16] :
                            select_mux_byte_opcode == 2'b10 ? wire_opcode_enviar[15:8]  : wire_opcode_enviar[7:0];

wire wire_conta_contador_mux_byte_enviar;
wire wire_reset_contador_mux_byte_enviar;
wire [3:0] select_mux_byte_enviar;
/*contador utilizado como seletor do mux de byte enviar* /
contador_m #(8, 4) contador_byte_enviar
  (
   .clock(clock),
   .zera_as(wire_reset_contador_mux_byte_enviar),
   .zera_s(1'b0),
   .conta(wire_conta_contador_mux_byte_enviar),
   .Q(select_mux_byte_enviar),
   .fim(),
   .meio()
  );

wire [7:0] byte_enviar;
assign byte_enviar = (select_mux_byte_enviar == 4'd0) ? wire_pontos_aux[7:0] :
                     (select_mux_byte_enviar == 4'd1) ? {wire_opcode_mux_out, wire_quantidade_vidas, 3'b000} :
                     (select_mux_byte_enviar == 4'd2) ? {(wire_aste_renderizado ? {wire_aste_coor_x, wire_aste_coor_y} : 8'b0)} :
                     (select_mux_byte_enviar == 4'd3) ? byte_opcode_enviar :
                     (select_mux_byte_enviar == 4'd4) ? {(wire_tiro_renderizado ? {wire_tiro_coor_x, wire_tiro_coor_y} : 8'b0)} :
                     (select_mux_byte_enviar == 4'd5) ? byte_opcode_enviar : 
                     (select_mux_byte_enviar == 4'd6) ? {wire_saida_reg_jogada[1], wire_rco_intervalo_especial, wire_saida_reg_jogada[0], wire_rco_intervalo_tiro, wire_vidas, 3'b0} : 
                     (select_mux_byte_enviar == 4'd7) ? {4'd4, 4'd1} : {wire_pontos_aux[7:0]};

wire wire_conta_contador_rodape;
wire wire_reset_contador_rodape;
wire wire_rco_contador_rodape;

/*contador utilizado para mandar o rodapé* /
contador_m #(2, 2) contador_rodape
  (
   .clock(clock),
   .zera_as(wire_reset_contador_rodape),
   .zera_s(1'b0),
   .conta(wire_conta_contador_rodape),
   .Q(),
   .fim(wire_rco_contador_rodape),
   .meio()
  );

uart_tx #(3) UART_TX_INST (
    .i_Clock(clock),
    .i_Tx_DV(jogo_base_em_andamento ? wire_iniciar_transmissao_uart_tx : iniciar_transmissao), // sinal de iniciar a transmissão
    .i_Tx_Byte(jogo_base_em_andamento ? byte_enviar : tela_renderizar),                    // dado
    .o_Tx_Active(),                             // sinal que indica que a uart de transmitir dados está ocupada
    .o_Tx_Serial(saida_serial),
    .o_Tx_Done(wire_terminou_transmissao_de_byte)   // pronto
);
assign acabou_transmissao = wire_terminou_transmissao_de_byte;

/******************************************************************************************************************** /
/*********************************************UC_JOGO_PRINCIPAL****************************************************** /
/******************************************************************************************************************** /
wire wire_ocorreu_especial;
uc_jogo_principal uc_jogo_principal(
    /* inputs * /
    .clock(clock),
    .iniciar(iniciar),
    .reset(reset),
    .vidas(~wire_vidas),
    .fim_movimentacao_asteroides_e_tiros(wire_fim_movimentacao_asteroides_e_tiros), 
    .fim_registra_tiros(wire_tiro_registrado),
    .fim_registra_especial(wire_fim_registra_especial),
    .ocorreu_tiro(wire_ocorreu_tiro),
    .ocorreu_jogada(wire_ocorreu_jogada),
    .ocorreu_especial(wire_ocorreu_especial),
    .tiro(wire_saida_reg_jogada[0]),
    .especial(wire_saida_reg_jogada[1]),
    .rco_intervalo_especial(wire_rco_intervalo_especial),
    .rco_intervalo_tiro(wire_rco_intervalo_tiro),
    /* outputs * /
    .enable_reg_jogada(wire_enable_reg_jogada),
    .reset_reg_jogada(wire_reset_reg_jogada),
    .reset_pontuacao(wire_reset_pontuacao_uc_principal),
    .inicia_registra_tiros(wire_inicia_registra_tiros),
    .inicia_registra_especial(wire_inicia_registra_especial),
    .inicia_movimentacao_asteroides_e_tiros(wire_inicia_movimentacao_asteroides_e_tiros), 
    .reset_contador_asteroides(wire_reset_contador_asteroides_uc_principal),
    .reset_contador_tiro(wire_reset_contador_tiro_uc_principal),
    .reset_contador_vidas(wire_reset_contador_vidas),
    .reset_maquinas(wire_reset_maquinas),
    .pronto(gameover),
    .termina(wire_termina_uc_jogo_principal),
    .db_estado_jogo_principal(db_estado_jogo_principal)
);

contador_163 #(64) contador_intervalo_tiro  ( 
    /* inputs * /
    .clock(clock),
    .clr(wire_tiro_registrado || wire_reset_maquinas),
    .ld(1'b0),
    .ent(1'b1),
    .enp(1'b1), 
    .D(),
    .Max(64'd250),
    /*outputs* /
    .Q(),
    .rco(wire_rco_intervalo_tiro)
);

wire [1:0] wire_opcode_especial;
wire wire_enable_load_tiro_uc_registra_especial;
wire wire_select_mux_pos_uc_registra_especial;
wire [1:0] wire_select_mux_pos_tiro_uc_registra_especial;


/******************************************************************************************************************** /
/*********************************************UC_REGISTRA_ESPECIAL*************************************************** /
/******************************************************************************************************************** /

uc_registra_especial uc_registra_especial(
    /* inputs * /
    .clock(clock),
    .reset(wire_reset_maquinas),
    .registra_tiro_especial(wire_inicia_registra_especial), 
    .loaded_tiro(wire_tiro_renderizado),
    .rco_contador_tiro(wire_rco_contador_tiro),
    .rco_opcode(wire_rco_contador_especial),
    /* outputs * /
    .reset_contador_tiro(wire_reset_contador_tiro_uc_registra_especial), 
    .reset_contador_especial(wire_reset_contador_especial_uc_registra_especial),
    .reset_intervalo_especial(wire_reset_intervalo_especial),
    .enable_mem_tiro(wire_enable_mem_tiro_uc_registra_especial), 
    .select_mux_pos(wire_select_mux_pos_tiro_uc_registra_especial),
    .new_load(wire_new_load_uc_registra_especial),
    .enable_load_tiro(wire_enable_load_tiro_uc_registra_especial),
    .conta_contador_opcode(wire_conta_contador_opcode),
    .conta_contador_tiro(wire_conta_contador_tiro_uc_registra_especial),
    .especial_registrado(wire_fim_registra_especial), 
    .select_mux_especial_opcode(wire_select_mux_especial_opcode),
    .db_estado_registra_tiro_especial(db_estado_registra_tiro_especial)
);


mux_reg_jogada mux_jogada(
    .select_mux_jogada (wire_saida_reg_jogada[5:2]),
    /* output * /
    .saida_mux       (wire_opcode_mux_out)
);

/**********mux para o seletor do opcode para registrar o tiro*************** /
wire [1:0] wire_opcode_registra_tiro;
assign wire_opcode_registra_tiro = wire_select_mux_especial_opcode ?  wire_opcode_contador_especial : wire_opcode_mux_out;

wire wire_rco_contador_especial;
wire [1:0] wire_opcode_contador_especial;

contador_m #(4, 2) contador_tiro_especial_opcode (
    /* inputs * /
    .clock(clock),
    .zera_as(wire_reset_contador_especial_uc_registra_especial || wire_reset_maquinas),
    .zera_s(1'b0),
    .conta(wire_conta_contador_opcode),
    /* outputs * /
    .Q(wire_opcode_contador_especial),
    .fim(wire_rco_contador_especial),
    .meio()
);

wire wire_rco_contador_tiro;
wire wire_rco_contador_asteroides;
wire wire_fim_move_tiros;
wire wire_fim_move_asteroides;
wire wire_fim_comparacao_asteroides_com_a_nave_e_tiros;
wire wire_fim_comparacao_tiros_e_asteroides;
wire wire_movimenta_tiro;
wire wire_sinal_movimenta_asteroides;
wire wire_sinal_compara_tiros_e_asteroides_uc_coordena_asteroides_tiros;
wire wire_sinal_compara_asteroides_com_a_nave_e_tiro;
wire wire_sinal_compara_tiros_e_asteroide_uc_compara_asteroides_com_nave_e_tiros;
wire wire_inicia_gera_frame_uc_coordena_asteroides_tiros;
wire wire_fim_gera_frame_uc_gera_frame;
wire wire_pausar_renderizacao;
wire wire_gera_asteroide;
wire wire_rco_contador_gera_aste;
wire reset_contador_gera_aste;


/******************************************************************************************************************** /
/**************************************************DIFICULDADES****************************************************** /
/******************************************************************************************************************** /
wire wire_rco_contador_movimenta_tiro;
wire wire_rco_contador_movimenta_asteroide;
wire wire_reset_contador_movimenta_tiro;
wire wire_reset_contador_movimenta_asteroide;



parameter tempo_especial = 64'd20000;

wire [63:0] tempo_gera_aste;
wire [63:0] tempo_move_aste;
wire [63:0] tempo_move_tiro;


contador_163_dificuldades #(64, 10000) contador_163_dificuldades( 
    .clock(clock), 
    .clr(iniciar || wire_reset_maquinas), 
    .ld(1'b0), 
    .ent(1'b1), 
    .enp(1'b1), 
    .D(),
    .Q(), 
    .rco(),
    .tempo_gera_aste(tempo_gera_aste),
    .tempo_move_aste(tempo_move_aste),
    .tempo_move_tiro(tempo_move_tiro)
);


contador_163 #(64) contador_gera_asteroide  ( 
    /* inputs * /
    .clock(clock), 
    .clr(wire_reset_contador_gera_asteroide), 
    .ld(1'b0), 
    .ent(1'b1), 
    .enp(wire_conta_contador_gera_asteroide), 
    .D(),
    .Max(tempo_gera_aste),
    /* outputs * /
    .Q(),
    .rco(wire_rco_contador_gera_aste)
);

contador_163 #(64) contador_movimenta_tiro  ( 
    /* inputs * /
    .clock(clock), 
    .clr(wire_reset_contador_movimenta_tiro), 
    .ld(1'b0), 
    .ent(1'b1), 
    .enp(1'b1), 
    .D(),
    .Max(tempo_move_tiro),
    /*outputs* /
    .Q(),
    .rco(wire_rco_contador_movimenta_tiro)
);

contador_163 #(64) contador_movimenta_asteroide  ( 
    /* inputs * /
    .clock(clock), 
    .clr(wire_reset_contador_movimenta_asteroide), 
    .ld(1'b0), 
    .ent(1'b1), 
    .enp(1'b1), 
    .D(),
    .Max(tempo_move_aste),
    /*outputs* /
    .Q(),
    .rco(wire_rco_contador_movimenta_asteroide)
);

wire wire_reset_intervalo_especial;
wire wire_rco_intervalo_especial;
contador_163 #(64) contador_especial_163  ( 
    /* inputs * /
    .clock(clock), 
    .clr(wire_reset_intervalo_especial || wire_reset_maquinas), 
    .ld(1'b0), 
    .ent(1'b1), 
    .enp(1'b1), 
    .D(),
    .Max(tempo_especial),
    /*outputs* /
    .Q(),
    .rco(wire_rco_intervalo_especial)
);


assign db_especial = wire_rco_intervalo_especial;


/******************************************************************************************************************** /
/*********************************************UC_COORDENA_ASTEROIDES************************************************* /
/******************************************************************************************************************** /
wire wire_enviar_dados_uc_coordena_asteroides_tiros;
uc_coordena_asteroides_tiros uc_coordena_asteroides_tiros(
    /* inputs * /
    .clock(clock),
    .reset(wire_reset_maquinas),
    .move_tiro_e_asteroides(wire_inicia_movimentacao_asteroides_e_tiros),
    .rco_contador_movimenta_tiros(wire_rco_contador_movimenta_tiro),
    .rco_contador_movimenta_asteroides(wire_rco_contador_movimenta_asteroide),
    .fim_move_tiros(wire_fim_move_tiros),
    .fim_move_asteroides(wire_fim_move_asteroides),
    .fim_comparacao_asteroides_com_a_nave_e_tiros(wire_fim_comparacao_asteroides_com_a_nave_e_tiros),
    .fim_comparacao_tiros_e_asteroides(wire_fim_comparacao_tiros_e_asteroides),
    .fim_gera_frame(wire_fim_gera_frame_uc_gera_frame),
    .fim_gera_asteroide(wire_fim_gera_asteroide),
    // .fim_transmissao_de_dados(wire_terminou_de_enviar_dados_uc_envia_dados), // com a uart tx
    .fim_transmissao_de_dados(1'b1), // sem a uart tx
    .gera_aste(wire_rco_contador_gera_aste),
    .termina_operacao(wire_termina_uc_jogo_principal),
    /* outputs * /
    .movimenta_tiro(wire_movimenta_tiro),
    .sinal_movimenta_asteroides(wire_sinal_movimenta_asteroides),
    .sinal_compara_tiros_e_asteroides(wire_sinal_compara_tiros_e_asteroides_uc_coordena_asteroides_tiros ),
    .sinal_compara_asteroides_com_a_nave_e_tiro(wire_sinal_compara_asteroides_com_a_nave_e_tiro),
    .fim_move_tiro_e_asteroides(wire_fim_movimentacao_asteroides_e_tiros),
    .gera_frame(wire_inicia_gera_frame_uc_coordena_asteroides_tiros),
    .pausar_renderizacao(wire_pausar_renderizacao),
    .gera_asteroide(wire_gera_asteroide),
    .reset_gerador_random(wire_reset_gerador_random),
    .enviar_dados(wire_enviar_dados_uc_coordena_asteroides_tiros),
    .db_estado_coordena_asteroides_tiros(db_estado_coordena_asteroides_tiros)
);

wire wire_reset_contador_asteroides_uc_gera_asteroide;
wire wire_conta_contador_asteroides_uc_gera_asteroide;
wire wire_enable_mem_aste_uc_gera_asteroide;
wire wire_enable_load_aste_uc_gera_asteroide;
wire wire_new_loaded_aste_uc_gera_asteroide;
wire wire_conta_contador_gera_asteroide;
wire wire_reset_contador_gera_asteroide;



/******************************************************************************************************************** /
/*********************************************UC_GERA_ASTEROIDE****************************************************** /
/******************************************************************************************************************** /

uc_gera_asteroide uc_gera_asteroide (
    /* inputs * /
    .clock(clock)        ,
    .reset(wire_reset_maquinas),
    .gera_asteroide(wire_gera_asteroide),      
    .rco_contador_asteroide(wire_rco_contador_asteroides),
    .asteroide_renderizado(wire_aste_renderizado),

    /* outputs * /
    .reset_contador_asteroide(wire_reset_contador_asteroides_uc_gera_asteroide),
    .conta_contador_asteroide(wire_conta_contador_asteroides_uc_gera_asteroide),
    .conta_contador_gera_asteroide(wire_conta_contador_gera_asteroide),
    .reset_contador_gera_asteroide(wire_reset_contador_gera_asteroide),
    .enable_mem_aste(wire_enable_mem_aste_uc_gera_asteroide),
    .enable_load_aste(wire_enable_load_aste_uc_gera_asteroide),
    .new_loaded_aste(wire_new_loaded_aste_uc_gera_asteroide),
    .fim_gera_asteroide(wire_fim_gera_asteroide),
    .db_uc_gera_asteroide(db_uc_gera_asteroide)
);


wire wire_conta_contador_asteroides_uc_gera_frame;
wire wire_conta_contador_tiro_uc_gera_frame;
wire wire_reset_contador_tiro_uc_gera_frame;
wire wire_reset_contador_asteroide_uc_gera_frame;
wire wire_clear_mem_frame;
wire wire_enable_mem_frame;
wire [1:0] wire_select_mux_gera_frame;



/******************************************************************************************************************** /
/*************************************************UC_GERA_FRAME****************************************************** /
/******************************************************************************************************************** /

uc_gera_frame uc_gera_frame (
        /*inputs* /
        .clock(clock),
        .reset(wire_reset_maquinas),
        .gera_frame(wire_inicia_gera_frame_uc_coordena_asteroides_tiros),
        .rco_contador_asteroides(wire_rco_contador_asteroides),
        .rco_contador_tiro(wire_rco_contador_tiro),
        .loaded_tiro(wire_tiro_renderizado),
        .loaded_asteroide(wire_aste_renderizado),
        /*outputs* /
        .conta_contador_asteroide(wire_conta_contador_asteroides_uc_gera_frame),
        .conta_contador_tiro(wire_conta_contador_tiro_uc_gera_frame),
        .reset_contador_tiro(wire_reset_contador_tiro_uc_gera_frame),
        .reset_contador_asteroide(wire_reset_contador_asteroide_uc_gera_frame),
        .clear_mem_frame(wire_clear_mem_frame),
        .enable_mem_frame(wire_enable_mem_frame),
        .fim_gera_frame(wire_fim_gera_frame_uc_gera_frame),
        .select_mux_gera_frame(wire_select_mux_gera_frame),
        .db_estado_uc_gera_frame(db_estado_uc_gera_frame)
);


wire [3:0] wire_entrada_x_memoria_frame;
wire [3:0] wire_entrada_y_memoria_frame;

assign wire_entrada_x_memoria_frame = (wire_select_mux_gera_frame == 2'b00) ? wire_aste_coor_x : 
                                      (wire_select_mux_gera_frame == 2'b01) ? wire_tiro_coor_x : 
                                      (wire_select_mux_gera_frame == 2'b10) ? 4'b0111          : wire_saida_contador_frame ;
 
assign wire_entrada_y_memoria_frame = (wire_select_mux_gera_frame == 2'b00) ? wire_aste_coor_y : 
                                      (wire_select_mux_gera_frame == 2'b01) ? wire_tiro_coor_y :
                                      (wire_select_mux_gera_frame == 2'b10) ? 4'b0111          : wire_saida_contador_frame;

memoria_frame memoria_frame(
    /*inputs* /
    .coor_x(wire_entrada_y_memoria_frame),
    .coor_y(wire_entrada_x_memoria_frame),
    .clk   (clock),
    .clear(wire_clear_mem_frame),
    .we   (wire_enable_mem_frame),
    /*outputs* /
    .saida_x(matriz_x),
    .saida_y(matriz_y)
);

wire wire_rco_contador_frame;
wire wire_conta_contador_frame;
wire wire_reset_contador_frame;



/******************************************************************************************************************** /
/*********************************************UC_RENDERIZA****************************************************** /
/******************************************************************************************************************** /

wire [3:0] wire_saida_contador_frame; 
wire [3:0] entrada_y_mem_frame;

uc_renderiza uc_renderiza (
        /*inputs* /
        .clock(clock),
        .reset(wire_reset_maquinas),
        .pausar_renderizacao(wire_pausar_renderizacao),
        .rco_contador_frame(wire_rco_contador_frame),
        /*outputs* /
        .reset_contador_frame(wire_reset_contador_frame),
        .conta_contador_frame(wire_conta_contador_frame),
        .db_estado_uc_renderiza(db_estado_uc_renderiza)
);

 contador_m #(15, 4) contador_renderiza(
    /*inputs* /
   .clock(clock),
   .zera_as(wire_reset_contador_frame),
   .zera_s(1'b0),
   .conta(wire_conta_contador_frame),
   /*outputs* /
   .Q(wire_saida_contador_frame),
   .fim(wire_rco_contador_frame),
   .meio()
  );





/******************************************************************************************************************** /
/*************************************UC_COMPARA_TIROS_E_ASTEROIDES************************************************** /
/******************************************************************************************************************** /

wire wire_posicao_tiro_igual_asteroide;
wire wire_tiro_renderizado;
wire wire_aste_renderizado;
wire wire_reset_contador_asteroides_uc_compara_tiros_e_asteroides;
wire wire_reset_contador_tiros_uc_compara_tiros_e_asteroides;
wire wire_enable_load_tiro_uc_compara_tiros_e_asteroides;
wire wire_enable_load_asteroide_uc_compara_tiros_e_asteroides;
wire wire_new_loaded_tiro_uc_compara_tiros_e_asteroides;
wire wire_new_loaded_asteroide_uc_compara_tiros_e_asteroides;
wire wire_new_destruido_asteroide_uc_compara_tiros_e_asteroides;
wire wire_incrementa_pontos_uc_compara_tiros_e_asteroides;
wire wire_conta_contador_asteroides_uc_compara_tiros_e_asteroides;
wire wire_conta_contador_tiros_uc_compara_tiros_e_asteroides;

uc_compara_tiros_e_asteroides uc_compara_tiros_e_asteroides (
    /* inputs * /
    .clock(clock),
    .reset(wire_reset_maquinas),
    .compara_tiros_e_asteroides(wire_sinal_compara_tiros_e_asteroides_uc_coordena_asteroides_tiros |
                                wire_sinal_compara_tiros_e_asteroide_uc_compara_asteroides_com_nave_e_tiros
                                ),
    .posicao_tiro_igual_asteroide(wire_posicao_tiro_igual_asteroide),
    .rco_contador_asteroides(wire_rco_contador_asteroides),
    .rco_contador_tiros(wire_rco_contador_tiro),
    .tiro_renderizado(wire_tiro_renderizado),
    .aste_renderizado(wire_aste_renderizado),
    /* outputs * /
    .reset_contador_asteroides(wire_reset_contador_asteroides_uc_compara_tiros_e_asteroides),
    .reset_contador_tiros(wire_reset_contador_tiros_uc_compara_tiros_e_asteroides),
    .enable_load_tiro(wire_enable_load_tiro_uc_compara_tiros_e_asteroides),
    .enable_load_asteroide(wire_enable_load_asteroide_uc_compara_tiros_e_asteroides),
    .loaded_tiro(wire_new_loaded_tiro_uc_compara_tiros_e_asteroides),
    .loaded_asteroide(wire_new_loaded_asteroide_uc_compara_tiros_e_asteroides),
    .asteroide_destruido(wire_new_destruido_asteroide_uc_compara_tiros_e_asteroides),
    .conta_contador_asteroides(wire_conta_contador_asteroides_uc_compara_tiros_e_asteroides),
    .conta_contador_tiros(wire_conta_contador_tiros_uc_compara_tiros_e_asteroides),
    .incrementa_pontos(wire_incrementa_pontos_uc_compara_tiros_e_asteroides),
    .s_fim_comparacao(wire_fim_comparacao_tiros_e_asteroides),
    .db_estado_compara_tiros_e_asteroide(db_estado_compara_tiros_e_asteroide)
);


/******************************************************************************************************************** /
/*************************************************UC_MOVE_TIROS****************************************************** /
/******************************************************************************************************************** /

wire [1:0] wire_opcode_tiro;
wire wire_x_borda_max_tiro;
wire wire_y_borda_max_tiro;
wire wire_x_borda_min_tiro;
wire wire_y_borda_min_tiro;
wire [1:0] wire_select_mux_pos_tiro_uc_move_tiros;
wire wire_select_mux_coor_tiro_uc_move_tiros;
wire wire_select_soma_sub_uc_move_tiros;
wire wire_reset_contador_tiro_uc_move_tiros;
wire wire_conta_contador_tiro_uc_move_tiros;
wire wire_enable_mem_tiro_uc_move_tiros;
wire wire_enable_load_tiro_uc_move_tiros;
wire wire_new_loaded_tiro_uc_move_tiros;

uc_move_tiros uc_move_tiros (
    /* inputs * /
    .clock(clock),
    .movimenta_tiro(wire_movimenta_tiro),
    .reset(wire_reset_maquinas),
    .opcode_tiro(wire_opcode_tiro),
    .loaded_tiro(wire_tiro_renderizado),
    .rco_contador_tiro(wire_rco_contador_tiro),
    .x_borda_max_tiro(wire_x_borda_max_tiro),
    .y_borda_max_tiro(wire_y_borda_max_tiro),
    .x_borda_min_tiro(wire_x_borda_min_tiro),
    .y_borda_min_tiro(wire_y_borda_min_tiro), 
    /* outputs * /
    .select_mux_pos_tiro (wire_select_mux_pos_tiro_uc_move_tiros),   
    .select_mux_coor_tiro(wire_select_mux_coor_tiro_uc_move_tiros),   
    .select_soma_sub(wire_select_soma_sub_uc_move_tiros),  
    .reset_contador_tiro(wire_reset_contador_tiro_uc_move_tiros),
    .conta_contador_tiro(wire_conta_contador_tiro_uc_move_tiros), 
    .reset_contador_movimenta_tiro(wire_reset_contador_movimenta_tiro),
    .enable_mem_tiro(wire_enable_mem_tiro_uc_move_tiros), 
    .enable_load_tiro(wire_enable_load_tiro_uc_move_tiros),
    .new_loaded(wire_new_loaded_tiro_uc_move_tiros),                
    .movimentacao_concluida_tiro(wire_fim_move_tiros), 
    .db_estado_move_tiros(db_estado_move_tiros)
);



/******************************************************************************************************************** /
/**********************************UC_COMPARA_ASTEROIDES_COM_NAVE_E_TIROS******************************************** /
/******************************************************************************************************************** /
wire wire_posicao_asteroide_igual_nave;
wire wire_new_loaded_asteroide_uc_compara_asteroides_com_nave_e_tiros;
wire wire_new_destruido_asteroide_uc_compara_asteroides_com_nave_e_tiros;
wire wire_enable_load_asteroides_uc_compara_asteroides_com_nave_e_tiros;
wire wire_reset_contador_asteroides_uc_compara_asteroides_com_nave_e_tiros;
wire wire_conta_contador_asteroides_uc_compara_asteroides_com_nave_e_tiros;

uc_compara_asteroides_com_nave_e_tiros uc_compara_asteroides_com_nave_e_tiros (
    /* inputs * /
    .clock(clock),
    .reset(wire_reset_maquinas),
    .iniciar_comparacao_tiros_nave_asteroides(wire_sinal_compara_asteroides_com_a_nave_e_tiro),
    .posicao_asteroide_igual_nave(wire_posicao_asteroide_igual_nave),
    .ha_vidas(~wire_vidas),
    .rco_contador_asteroides(wire_rco_contador_asteroides),
    .fim_compara_tiros_e_asteroides(wire_fim_comparacao_tiros_e_asteroides),
    .loaded_asteroide(wire_aste_renderizado),
    .destruido_asteroide(wire_destruido_aste),
    /* outputs * /
    .enable_decrementador(wire_enable_decrementador),
    .new_loaded_asteroide(wire_new_loaded_asteroide_uc_compara_asteroides_com_nave_e_tiros),
    .new_destruido_asteroide(wire_new_destruido_asteroide_uc_compara_asteroides_com_nave_e_tiros),
    .fim_compara_asteroides_com_tiros_e_nave(wire_fim_comparacao_asteroides_com_a_nave_e_tiros),
    .enable_load_asteroide(wire_enable_load_asteroides_uc_compara_asteroides_com_nave_e_tiros),
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*/
